# Fritzing sketch detectorbeacons (saved by Fritzing 0.9.3b)
circuit board: 10.0429cm x 5.65554cm
breadboards: 1

parts:
  xbee = XBee Explorer Regulated
  BT_MH-10 = Bluetooth HC-05 Macho
  Componente2 = Arduino Uno (Rev3) - ICSP

nets:
  N1: xbee.DIN, Componente2.D9_PWM
  N2: xbee.DOUT, Componente2.D11_PWM/MOSI
  3.3V: xbee.3.3V, BT_MH-10.VCC, Componente2.3V3
  GND: xbee.GND, BT_MH-10.GND, Componente2.GND
  N3: BT_MH-10.TXD, Componente2.D7
  N4: BT_MH-10.RXD, Componente2.D5_PWM
